# Fritzing sketch final (saved by Fritzing 0.8.7b)
breadboards: 1

parts:
  Q1 = Basic FET P-Channel [package="TO220 [THT]"]
  Q2 = Basic FET P-Channel [package="TO220 [THT]"]
  M2 = DC Motor
  BAT1 = BC9VPC [package=bc9vpc]
  Part1 = Arduino Uno (Rev3)
  Part2 = SRF05 Ultrasonic Rangefinder
  R1 = Resistor [tolerance=±5% resistance=220 package=THT]
  M1 = DC Motor
  R2 = Resistor [tolerance=±5% resistance=220 package=THT]

nets:
  N1: Q1.gate, R1.Pin_1
  N2: Q1.drain, M1.pin_2
  N3: Q1.source, Q2.source, M2.pin_2, BAT1.V+, Part2.GND, M1.pin_1
  N4: Q2.gate, R2.Pin_1
  N5: Q2.drain, M2.pin_1
  N6: BAT1.V-, Part2.VCC
  N7: Part1.D9_PWM, Part2.Trig
  N8: Part1.D10_PWM/SS, Part2.Echo
  N9: Part1.D3_PWM, R1.Pin_0
  N10: Part1.D4, R2.Pin_0
